# Fritzing sketch sun-tracker (saved by Fritzing 0.9.4)

parts:
  MH-ET_Live_Minikit_for_ESP1 = MH-ET Live Minikit for ESP32
  R1 = Resistor [tolerance=±5% resistance=4.7k package="0805 [SMD]"]
  R2 = Resistor [tolerance=±5% resistance=4.7k package="0805 [SMD]"]
  Q1 = NPN-Transistor [part_number=BC172 package="TO92 [THT]"]
  Q2 = NPN-Transistor [part_number=BC172 package="TO92 [THT]"]
  OMRON1 = OMRON PCB Power Relay – G5LE [part_number="RELE 1" package=THT]
  OMRON2 = OMRON PCB Power Relay – G5LE [part_number="RELE 2" package=THT]
  JP1 = Header 2 [package=screwterminal-3.5mm-2_lock]
  JP2 = Header 2 [package=screwterminal-3.5mm-2_lock]
  JP3 = Header 2 [part_number=PDR2 package=screwterminal-3.5mm-2_lock]
  JP4 = Header 2 [package=screwterminal-3.5mm-2_lock]
  JP5 = Header 2 [part_number=PDR1 package=screwterminal-3.5mm-2_lock]
  R3 = Resistor [tolerance=±5% resistance=10k package="0805 [SMD]"]
  R4 = Resistor [tolerance=±5% resistance=10k package="0805 [SMD]"]
  R5 = Photocell (LDR) [package=THT]  # not connected
  R6 = Photocell (LDR) [package=THT]  # not connected
  S1 = SPST Switch [package=switche-dpdt]  # not connected
  S2 = SPST Switch [package=switche-dpdt]  # not connected
  JP6 = Header 2 [part_number=RUNEND2 package=screwterminal-3.5mm-2_lock]
  JP7 = Header 2 [part_number=RUNEND1 package=screwterminal-3.5mm-2_lock]
  M1 = DC Motor  # not connected

nets:
  N1: MH-ET_Live_Minikit_for_ESP1.GND, Q1.E, Q2.E, R3.Pin_1, R4.Pin_1, JP6.1, JP7.1
  N2: MH-ET_Live_Minikit_for_ESP1.IO35, JP5.1, R4.Pin_0
  N3: MH-ET_Live_Minikit_for_ESP1.IO33, R1.Pin_1
  N4: MH-ET_Live_Minikit_for_ESP1.IO34, JP3.1
  N5: MH-ET_Live_Minikit_for_ESP1.TMS, R2.Pin_1
  N6: MH-ET_Live_Minikit_for_ESP1.3.3V, JP3.2, JP5.2
  N7: MH-ET_Live_Minikit_for_ESP1.VCC, OMRON1.COIL1, OMRON2.COIL1
  N8: MH-ET_Live_Minikit_for_ESP1.IO27, JP6.2
  N9: MH-ET_Live_Minikit_for_ESP1.IO32, JP7.2
  N10: R2.Pin_0, Q2.B
  N11: Q1.C, OMRON2.COIL2
  N12: Q2.C, OMRON1.COIL2
  N13: OMRON1.A, JP2.1
  N14: OMRON1.C, JP1.2
  N15: OMRON1.B, JP1.1
  N16: OMRON2.A, JP4.2
  N17: OMRON2.C, JP4.1
  N18: OMRON2.B, JP2.2

notes:
  +3.3V
  +5V
  Motor Vcc
  Motor Gnd
  Normally open

custom parts:
  MH-ET Live Minikit for ESP32: MH-ET Live Minikit for ESP32 ( http://mh.nodebb.com/topic/8/mh-et-live-minikit-for-esp32/2/) PCB footprint is invalid.
